# Fritzing sketch SSCI_envirobox (saved by Fritzing 1.0.3b)
perfboards: 1

parts:
  Adafruit_RP2040_CAN_Bus_Feather1 = Adafruit RP2040 CAN Bus Feather [part_number=#5724]
  PCA1 = Adafruit PCA9548 8-Channel STEMMA QT / Qwiic I2C Multiplexer [part_number=5626]
  Part1 = Adafruit AHT20 Temperature and Humidity Sensor [part_number="Adafruit #4566"]
  Part2 = Adafruit BMP390 [part_number="Adafruit #4816"]
  Part5 = Adafruit BNO085 9-DOF Orientation IMU Fusion [part_number="Addfruit #4754"]
  JP1 = Header 4 [package=jst-4-pth]
  JP3 = Header 4 [package=jst-4-pth]
  JP4 = Header 4 [package=jst-4-pth]
  LLC1 = Logic Level Converter [package="Breakout board"]
  A1 = mini boost module
  J1 = 2.1mm Barrel Jack with Terminal Block

nets:
  GND: Adafruit_RP2040_CAN_Bus_Feather1.GND, PCA1.GND, Part1.GND, Part2.GND, Part5.GND, JP1.4, JP3.4, JP4.4, LLC1.L-GND, LLC1.H-GND, A1.Pin_1, A1.Pin_4
  VCC: Adafruit_RP2040_CAN_Bus_Feather1.+3V3, PCA1.VCC, Part5.VCC, LLC1.LV, A1.Pin_2
  N1: Adafruit_RP2040_CAN_Bus_Feather1.SDA, PCA1.SDA, Part5.SDA/MISO/TX
  N2: Adafruit_RP2040_CAN_Bus_Feather1.SCL, PCA1.SCL, Part5.SCL/SCK/RX
  N3: Adafruit_RP2040_CAN_Bus_Feather1.A2, LLC1.LV4
  N4: Adafruit_RP2040_CAN_Bus_Feather1.A1, LLC1.LV3
  N5: Adafruit_RP2040_CAN_Bus_Feather1.A0, LLC1.LV2
  VCC_2: PCA1.VCCIO, Part1.VCC, Part2.VCC
  N6: PCA1.1SDA, Part1.SDA
  N7: PCA1.1SCL, Part1.SCL
  N8: PCA1.2SDA, Part2.SDI/SDA
  N9: PCA1.2SCL, Part2.SCK/SCL
  N10: JP1.1, JP3.1, JP4.1, J1.POS
  N11: JP1.2, JP3.2, JP4.2, J1.NEG
  N12: JP1.3, LLC1.HV2
  N13: JP3.3, LLC1.HV4
  N14: JP4.3, LLC1.HV3
  N15: LLC1.HV, A1.Pin_3

custom parts:
  Adafruit RP2040 CAN Bus Feather: If you'd like quickly get started with CAN bus interfacing, with no soldering required, our Adafruit RP2040 CAN Bus Feather comes ready-to-rock with a microcontroller, CAN chipset, and terminal blocks for instant gratification. The controller used is the MCP25625 (aka an MCP2515 with built-in transceiver), an extremely popular and well-supported chipset that has drivers in Arduino and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
  Adafruit PCA9548 8-Channel STEMMA QT / Qwiic I2C Multiplexer: You just found the perfect I2C sensor, available in a handy chainable Qwiic, or STEMMA QT package, and you want to wire up two or three or more of them to your microcontroller when you realize "Uh oh, this chip has a fixed I2C address, and from what I know about I2C, you cannot have two devices with the same address on the same SDA/SCL pins!" Are you out of luck? You would be, if you didn't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
  Adafruit AHT20 Temperature and Humidity Sensor: The AHT20 is a nice but inexpensive temperature and humidity sensor from the same folks that brought us the DHT22. You can take sensor readings as often as you like, and it uses standard I2C so its super easy to use with any Arduino or Linux/Raspberry Pi board. This sensor has a typical accuracy of +- 2% relative humidity, and +-0.3 °C. There is only one I2C address so its not a good option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
  Adafruit BMP390: Bosch has been a leader in barometric pressure sensors, from the BMP085. BMP180, BMP280, BMP388... now we've got the next generation, the Adafruit BMP390 Precision Barometric Pressure and Altimeter Breakout. As you would expect, this sensor is similar to its earlier versions but even better. The BMP390 has better precision than ever, which makes it excellent for environmental sensing or as a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
  Logic Level Converter: 5V to/from 3.3V logic level converter
  mini boost module: mini boost module.
